# Fritzing sketch Circuitry (saved by Fritzing 0.8.5b)

parts:
  Arduino_Mega_2560_(Rev3) = Arduino Mega 2560 (Rev3)
  J_RR = Basic Servo
  J_RL = Basic Servo
  J_FR = Basic Servo
  J_FL = Basic Servo
  FrontMC = Dual VNH2SP30 Motor Driver [part_number="Dual VNH5019 Motor Driver Shield for Arduino"]
  Rear_MC = Dual VNH2SP30 Motor Driver [part_number="Dual VNH5019 Motor Driver Shield for Arduino"]
  M_RL = DC Motor
  M_FL = DC Motor
  M_FR = DC Motor
  M_RR = DC Motor
  S_R = Round Pushbutton
  S_L = Round Pushbutton
  USD1 = HC-SR04 Ultrasonic Sensor [part_number=HC-SR04]
  USD2 = HC-SR04 Ultrasonic Sensor [part_number=HC-SR04]
  USD3 = HC-SR04 Ultrasonic Sensor [part_number=HC-SR04]
  USD4 = HC-SR04 Ultrasonic Sensor [part_number=HC-SR04]
  USD5 = HC-SR04 Ultrasonic Sensor [part_number=HC-SR04]
  USD7 = HC-SR04 Ultrasonic Sensor [part_number=HC-SR04]
  USD6 = HC-SR04 Ultrasonic Sensor [part_number=HC-SR04]
  USD8 = HC-SR04 Ultrasonic Sensor
  GPS = Adafruit Ultimate GPS Breakout

nets:
  N1: Arduino_Mega_2560_(Rev3).A0, Rear_MC.2CS
  N2: Arduino_Mega_2560_(Rev3).A1, Rear_MC.1CS
  N3: Arduino_Mega_2560_(Rev3).A2, FrontMC.2CS
  N4: Arduino_Mega_2560_(Rev3).A3, FrontMC.1CS
  GND: Arduino_Mega_2560_(Rev3).GND, J_RR.gnd, J_RL.gnd, J_FR.gnd, J_FL.gnd, FrontMC.GND, Rear_MC.GND, S_R.leg1, S_L.leg1, USD1.GND, USD2.GND, USD3.GND, USD4.GND, USD5.GND, USD7.GND, USD6.GND, USD8.GND, GPS.GND
  N5: Arduino_Mega_2560_(Rev3).D12_PWM, Rear_MC.2PWM
  N6: Arduino_Mega_2560_(Rev3).D11_PWM, Rear_MC.PWM
  N7: Arduino_Mega_2560_(Rev3).D10_PWM, FrontMC.2PWM
  N8: Arduino_Mega_2560_(Rev3).D9_PWM, FrontMC.PWM
  N9: Arduino_Mega_2560_(Rev3).D8_PWM, J_RR.pulse
  12V: Arduino_Mega_2560_(Rev3).VIN, FrontMC.VIN, Rear_MC.VIN
  N10: Arduino_Mega_2560_(Rev3).D0_RX0, GPS.TX
  N11: Arduino_Mega_2560_(Rev3).D1_TX0, GPS.RX
  N12: Arduino_Mega_2560_(Rev3).D5_PWM, J_FL.pulse
  N13: Arduino_Mega_2560_(Rev3).D6_PWM, J_FR.pulse
  N14: Arduino_Mega_2560_(Rev3).D7_PWM, J_RL.pulse
  N15: Arduino_Mega_2560_(Rev3).D22, FrontMC.1DIAG/EN
  N16: Arduino_Mega_2560_(Rev3).D23, FrontMC.2DIAG/EN
  N17: Arduino_Mega_2560_(Rev3).D24, Rear_MC.1DIAG/EN
  N18: Arduino_Mega_2560_(Rev3).D25, Rear_MC.2DIAG/EN
  N19: Arduino_Mega_2560_(Rev3).D26, FrontMC.1INa
  N20: Arduino_Mega_2560_(Rev3).D27, FrontMC.2INb#142
  N21: Arduino_Mega_2560_(Rev3).D28, Rear_MC.1INa
  N22: Arduino_Mega_2560_(Rev3).D29, Rear_MC.2INb#142
  N23: Arduino_Mega_2560_(Rev3).D30, FrontMC.1INb
  N24: Arduino_Mega_2560_(Rev3).D31, FrontMC.2INb#143
  N25: Arduino_Mega_2560_(Rev3).D32, Rear_MC.1INb
  N26: Arduino_Mega_2560_(Rev3).D33, Rear_MC.2INb#143
  N27: Arduino_Mega_2560_(Rev3).D34, S_L.leg0
  N28: Arduino_Mega_2560_(Rev3).D35, S_R.leg0
  N29: Arduino_Mega_2560_(Rev3).D38, USD1.Echo
  N30: Arduino_Mega_2560_(Rev3).D39, USD1.Trig
  N31: Arduino_Mega_2560_(Rev3).D40, USD2.Echo
  N32: Arduino_Mega_2560_(Rev3).D41, USD2.Trig
  N33: Arduino_Mega_2560_(Rev3).D42, USD3.Echo
  N34: Arduino_Mega_2560_(Rev3).D43, USD3.Trig
  N35: Arduino_Mega_2560_(Rev3).D44, USD4.Echo
  N36: Arduino_Mega_2560_(Rev3).D45, USD4.Trig
  N37: Arduino_Mega_2560_(Rev3).D46, USD5.Echo
  N38: Arduino_Mega_2560_(Rev3).D47, USD5.Trig
  N39: Arduino_Mega_2560_(Rev3).D48, USD6.Echo
  N40: Arduino_Mega_2560_(Rev3).D49, USD6.Trig
  N41: Arduino_Mega_2560_(Rev3).D50, USD7.Echo
  N42: Arduino_Mega_2560_(Rev3).D51, USD7.Trig
  N43: Arduino_Mega_2560_(Rev3).D52, USD8.Echo
  N44: Arduino_Mega_2560_(Rev3).D53, USD8.Trig
  5V: J_RR.vcc, J_RL.vcc, J_FR.vcc, J_FL.vcc, FrontMC.+5V_(IN), Rear_MC.+5V_(IN), USD1.VCC, USD2.VCC, USD3.VCC, USD4.VCC, USD5.VCC, USD7.VCC, USD6.VCC, USD8.VCC, GPS.VIN
  N45: FrontMC.OUT_1A, M_RL.pin_1
  N46: FrontMC.OUT_1B, M_RL.pin_2
  N47: FrontMC.OUT_2A, M_FL.pin_1
  N48: FrontMC.OUT_2B, M_FL.pin_2
  N49: Rear_MC.OUT_1A, M_FR.pin_1
  N50: Rear_MC.OUT_1B, M_FR.pin_2
  N51: Rear_MC.OUT_2A, M_RR.pin_1
  N52: Rear_MC.OUT_2B, M_RR.pin_2

notes:
  Intended motor drivers are the Pololu Dual VNH5019 Motor Driver Shield for Arduino. Part file not available. Wiring and control is similar to the part shown.
  Also note that logic ground connection is not shown.
  http://www.pololu.com/product/2507
  Robo-Magellan, Arduino Hardware Interface, 2

custom parts:
  HC-SR04 Ultrasonic Sensor: The HC-SR04 ultrasonic sensor uses sonar to determine distance to an object - just like bats or dolphins do. This module offers excellent range accuracy and stable readings in an easy-to-use package. It operation is not affected by sunlight or black material (although acoustically soft materials like cloth can be difficult to detect). Similar in performance to the SRF005 but with the low-price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
